// Logisim project Group 20.circ as structural Verilog
module main (
  input  in_1
);

  wire and_1_out, CLK_out, final_cu_4_1_branch, final_cu_4_1_branch_select, final_cu_4_1_jump_select,
       final_cu_4_1_offset_select, final_cu_4_1_reg_write, final_cu_4_1_src_a_select, final_cu_4_1_store,
       final_cu_4_1_wd_select, multiplexer_5_out, not_1_out, or_1_out, or_2_out;
  wire [3:0] final_cu_4_1_alu_select3, multiplexer_2_out, rom_1_data;
  wire [11:0] rom_1_data_2;
  wire [15:0] adder_1_out, adder_2_out, ALU_alu_output, bit_extender_1_out, bit_extender_2_out,
       bit_extender_3_out, multiplexer_1_out, multiplexer_3_out, multiplexer_4_out, multiplexer_6_out,
       R_Bank_rd_1, R_Bank_rd_2, ram_1_data, register_1_q;

  or or_1 (or_1_out, and_1_out, final_cu_4_1_jump_select);
  Multiplexer #(.width(16)) multiplexer_1 (
    .in0(adder_1_out), .in1(adder_2_out), .out(multiplexer_1_out), .sel(or_1_out));  // open: en
  Clock CLK (.out(CLK_out));
  Adder #(.width(16)) adder_1 (.a(register_1_q), .b(16'h1), .out(adder_1_out));  // open: cin, cout
  and and_1 (and_1_out, multiplexer_5_out, final_cu_4_1_branch);
  Register #(.width(16)) register_1 (.D(multiplexer_1_out), .Q(register_1_q), .clk(CLK_out), .clr(in_1));  // open: en
  ROM #(.addrWidth(16), .dataWidth(16)) rom_1 (.addr(register_1_q), .data({rom_1_data, rom_1_data_2}));  // open: sel
  final_cu_4 final_cu_4_1 (
    .I_15(rom_1_data[3]), .I_14(rom_1_data[2]), .I_13(rom_1_data[1]), .I_12(rom_1_data[0]),
    .Alu_Select0(final_cu_4_1_alu_select3[3]), .Alu_Select1(final_cu_4_1_alu_select3[2]),
    .Alu_Select2(final_cu_4_1_alu_select3[1]), .Alu_select3(final_cu_4_1_alu_select3[0]),
    .store(final_cu_4_1_store), .Src_A_Select(final_cu_4_1_src_a_select), .Wd_select(final_cu_4_1_wd_select),
    .reg_write(final_cu_4_1_reg_write), .offset_select(final_cu_4_1_offset_select),
    .Branch(final_cu_4_1_branch), .Branch_select(final_cu_4_1_branch_select),
    .Jump_select(final_cu_4_1_jump_select));
  Multiplexer #(.width(4)) multiplexer_2 (
    .in0(rom_1_data_2[3:0]), .in1(rom_1_data_2[11:8]), .out(multiplexer_2_out),
    .sel(final_cu_4_1_offset_select));  // open: en
  assign bit_extender_1_out = {{12{1'b0}}, multiplexer_2_out};  // Bit_Extender bit_extender_1
  register_bank R_Bank (
    .Write_data(multiplexer_6_out), .Select_Ra_1(rom_1_data_2[3:0]), .Select_Ra_2(rom_1_data_2[7:4]),
    .Write_enable(final_cu_4_1_reg_write), .Write_Register(rom_1_data_2[11:8]), .Rd_1(R_Bank_rd_1),
    .Rd_2(R_Bank_rd_2), .clock(CLK_out));
  assign bit_extender_2_out = {{4{rom_1_data_2[11]}}, rom_1_data_2};  // Bit_Extender bit_extender_2
  assign bit_extender_3_out = {{12{rom_1_data_2[11]}}, rom_1_data_2[11:8]};  // Bit_Extender bit_extender_3
  Multiplexer #(.width(16)) multiplexer_3 (
    .in0(bit_extender_1_out), .in1(R_Bank_rd_1), .out(multiplexer_3_out), .sel(final_cu_4_1_src_a_select));  // open: en
  Multiplexer #(.width(16)) multiplexer_4 (
    .in0(bit_extender_3_out), .in1(bit_extender_2_out), .out(multiplexer_4_out),
    .sel(final_cu_4_1_jump_select));  // open: en
  Multiplexer #(.enable("false")) multiplexer_5 (
    .in0(not_1_out), .in1(or_2_out), .out(multiplexer_5_out), .sel(final_cu_4_1_branch_select));
  Adder #(.width(16)) adder_2 (.a(register_1_q), .b(multiplexer_4_out), .out(adder_2_out));  // open: cin, cout
  not not_1 (not_1_out, or_2_out);
  Multiplexer #(.width(16)) multiplexer_6 (
    .in0(ram_1_data), .in1(ALU_alu_output), .out(multiplexer_6_out), .sel(final_cu_4_1_wd_select));  // open: en
  ALU ALU (
    .A(multiplexer_3_out), .B(R_Bank_rd_2), .alu_select(final_cu_4_1_alu_select3), .alu_output(ALU_alu_output));  // open: carry_in_adder, carry_in_sub, multiply_carry_in, divider_carry_in, in_6, carry_out_adder, carry_out_sub, multiply_carry_out, divider_Carry_out
  or or_2 (or_2_out, ALU_alu_output[0], ALU_alu_output[1], ALU_alu_output[2], ALU_alu_output[3], ALU_alu_output[4], ALU_alu_output[5], ALU_alu_output[6], ALU_alu_output[7], ALU_alu_output[8], ALU_alu_output[9], ALU_alu_output[10], ALU_alu_output[11], ALU_alu_output[12], ALU_alu_output[13], ALU_alu_output[14], ALU_alu_output[15]);
  RAM #(.addrWidth(16), .dataWidth(16), .bus("separate")) ram_1 (
    .addr(ALU_alu_output), .din(R_Bank_rd_1), .data(ram_1_data), .str(final_cu_4_1_store), .sel(1'b1),
    .clk(CLK_out), .ld(1'b1));  // open: clr

  // Notes on the sheet:
  //   contents of rom_1 (hex, n*v repeats v):
  //   b412 4123 4456 c003 5132 5456
endmodule

module subtractor (
  input  in_1,
  input  [15:0] in_2,
  input  [15:0] in_3,
  output [15:0] out_4,
  output out_5
);

  wire subtractor_1_bout, subtractor_2_bout, subtractor_3_bout, subtractor_4_bout, subtractor_5_bout,
       subtractor_6_bout, subtractor_7_bout, subtractor_8_bout, subtractor_9_bout, subtractor_10_bout,
       subtractor_11_bout, subtractor_12_bout, subtractor_13_bout, subtractor_14_bout, subtractor_15_bout;

  Subtractor #(.width(1)) subtractor_1 (.a(in_2[0]), .b(in_3[0]), .out(out_4[0]), .bin(in_1), .bout(subtractor_1_bout));
  Subtractor #(.width(1)) subtractor_2 (
    .a(in_2[1]), .b(in_3[1]), .out(out_4[1]), .bin(subtractor_1_bout), .bout(subtractor_2_bout));
  Subtractor #(.width(1)) subtractor_3 (
    .a(in_2[2]), .b(in_3[2]), .out(out_4[2]), .bin(subtractor_2_bout), .bout(subtractor_3_bout));
  Subtractor #(.width(1)) subtractor_4 (
    .a(in_2[3]), .b(in_3[3]), .out(out_4[3]), .bin(subtractor_3_bout), .bout(subtractor_4_bout));
  Subtractor #(.width(1)) subtractor_5 (
    .a(in_2[4]), .b(in_3[4]), .out(out_4[4]), .bin(subtractor_4_bout), .bout(subtractor_5_bout));
  Subtractor #(.width(1)) subtractor_6 (
    .a(in_2[5]), .b(in_3[5]), .out(out_4[5]), .bin(subtractor_5_bout), .bout(subtractor_6_bout));
  Subtractor #(.width(1)) subtractor_7 (
    .a(in_2[6]), .b(in_3[6]), .out(out_4[6]), .bin(subtractor_6_bout), .bout(subtractor_7_bout));
  Subtractor #(.width(1)) subtractor_8 (
    .a(in_2[7]), .b(in_3[7]), .out(out_4[7]), .bin(subtractor_7_bout), .bout(subtractor_8_bout));
  Subtractor #(.width(1)) subtractor_9 (
    .a(in_2[8]), .b(in_3[8]), .out(out_4[8]), .bin(subtractor_8_bout), .bout(subtractor_9_bout));
  Subtractor #(.width(1)) subtractor_10 (
    .a(in_2[9]), .b(in_3[9]), .out(out_4[9]), .bin(subtractor_9_bout), .bout(subtractor_10_bout));
  Subtractor #(.width(1)) subtractor_11 (
    .a(in_2[10]), .b(in_3[10]), .out(out_4[10]), .bin(subtractor_10_bout), .bout(subtractor_11_bout));
  Subtractor #(.width(1)) subtractor_12 (
    .a(in_2[11]), .b(in_3[11]), .out(out_4[11]), .bin(subtractor_11_bout), .bout(subtractor_12_bout));
  Subtractor #(.width(1)) subtractor_13 (
    .a(in_2[12]), .b(in_3[12]), .out(out_4[12]), .bin(subtractor_12_bout), .bout(subtractor_13_bout));
  Subtractor #(.width(1)) subtractor_14 (
    .a(in_2[13]), .b(in_3[13]), .out(out_4[13]), .bin(subtractor_13_bout), .bout(subtractor_14_bout));
  Subtractor #(.width(1)) subtractor_15 (
    .a(in_2[14]), .b(in_3[14]), .out(out_4[14]), .bin(subtractor_14_bout), .bout(subtractor_15_bout));
  Subtractor #(.width(1)) subtractor_16 (
    .a(in_2[15]), .b(in_3[15]), .out(out_4[15]), .bin(subtractor_15_bout), .bout(out_5));
endmodule

module ALU (
  input  [15:0] A,
  input  [15:0] B,
  input  [3:0] alu_select,
  input  carry_in_adder,
  input  carry_in_sub,
  input  in_6,
  input  [15:0] multiply_carry_in,
  input  [15:0] divider_carry_in,
  output [15:0] alu_output,
  output carry_out_adder,
  output carry_out_sub,
  output [15:0] multiply_carry_out,
  output [15:0] divider_Carry_out
);

  wire [15:0] adder_1_out, and_1_out, divider_1_out, multiplier_1_out, nor_1_out, not_1_out, or_1_out,
       subtractor_1_out;

  assign and_1_out = A & B;  // AND_Gate and_1, 16 bits wide
  assign not_1_out = ~A;  // NOT_Gate not_1, 16 bits wide
  assign or_1_out = A | B;  // OR_Gate or_1, 16 bits wide
  assign nor_1_out = ~(A | B);  // NOR_Gate nor_1, 16 bits wide
  Adder #(.width(16)) adder_1 (.a(A), .b(B), .out(adder_1_out), .cin(carry_in_adder), .cout(carry_out_adder));
  Subtractor #(.width(16)) subtractor_1 (
    .a(A), .b(B), .out(subtractor_1_out), .bin(carry_in_sub), .bout(carry_out_sub));
  Multiplier #(.width(16)) multiplier_1 (
    .a(A), .b(B), .out(multiplier_1_out), .cin(multiply_carry_in), .cout(multiply_carry_out));
  Divider #(.width(16)) divider_1 (
    .a(A), .b(B), .out(divider_1_out), .upper(divider_carry_in), .rem(divider_Carry_out));
  Multiplexer #(.select(4), .width(16)) multiplexer_1 (
    .in0(and_1_out), .in1(not_1_out), .in2(or_1_out), .in3(nor_1_out), .in4(adder_1_out),
    .in5(subtractor_1_out), .in6(multiplier_1_out), .in7(divider_1_out), .out(alu_output), .sel(alu_select),
    .en(in_6));  // open: in8, in9, in10, in11, in12, in13, in14, in15
endmodule

module register_bank (
  input  [3:0] Write_Register,
  input  [15:0] Write_data,
  input  [3:0] Select_Ra_1,
  input  [3:0] Select_Ra_2,
  input  Write_enable,
  input  clock,
  output [15:0] Rd_1,
  output [15:0] Rd_2
);

  wire and_1_out, and_2_out, and_3_out, and_4_out, and_5_out, and_6_out, and_7_out, and_8_out, and_9_out,
       and_10_out, and_11_out, and_12_out, and_13_out, and_14_out, and_15_out, and_16_out, decoder_1_out0,
       decoder_1_out1, decoder_1_out2, decoder_1_out3, decoder_1_out4, decoder_1_out5, decoder_1_out6,
       decoder_1_out7, decoder_1_out8, decoder_1_out9, decoder_1_out10, decoder_1_out11, decoder_1_out12,
       decoder_1_out13, decoder_1_out14, decoder_1_out15;
  wire [15:0] _0_q, _1_q, _2_q, _3_q, _4_q, _5_q, _6_q, _7_q, _8_q, _9_q, _10_q, _11_q, _12_q, _13_q, _14_q,
       _15_q;

  Decoder #(.select(4)) decoder_1 (
    .out0(decoder_1_out0), .out1(decoder_1_out1), .out2(decoder_1_out2), .out3(decoder_1_out3),
    .out4(decoder_1_out4), .out5(decoder_1_out5), .out6(decoder_1_out6), .out7(decoder_1_out7),
    .out8(decoder_1_out8), .out9(decoder_1_out9), .out10(decoder_1_out10), .out11(decoder_1_out11),
    .out12(decoder_1_out12), .out13(decoder_1_out13), .out14(decoder_1_out14), .out15(decoder_1_out15),
    .sel(Write_Register));  // open: en
  and and_1 (and_1_out, decoder_1_out0, Write_enable);
  and and_2 (and_2_out, decoder_1_out1, Write_enable);
  and and_3 (and_3_out, decoder_1_out2, Write_enable);
  and and_4 (and_4_out, decoder_1_out3, Write_enable);
  and and_5 (and_5_out, decoder_1_out4, Write_enable);
  and and_6 (and_6_out, decoder_1_out5, Write_enable);
  and and_7 (and_7_out, decoder_1_out6, Write_enable);
  and and_8 (and_8_out, decoder_1_out7, Write_enable);
  Register #(.width(16)) _0 (.D(Write_data), .en(and_1_out), .Q(_0_q), .clk(clock));  // open: clr
  Register #(.width(16)) _1 (.D(Write_data), .en(and_2_out), .Q(_1_q), .clk(clock));  // open: clr
  Register #(.width(16)) _2 (.D(Write_data), .en(and_3_out), .Q(_2_q), .clk(clock));  // open: clr
  Register #(.width(16)) _3 (.D(Write_data), .en(and_4_out), .Q(_3_q), .clk(clock));  // open: clr
  Register #(.width(16)) _4 (.D(Write_data), .en(and_5_out), .Q(_4_q), .clk(clock));  // open: clr
  Register #(.width(16)) _5 (.D(Write_data), .en(and_6_out), .Q(_5_q), .clk(clock));  // open: clr
  Register #(.width(16)) _6 (.D(Write_data), .en(and_7_out), .Q(_6_q), .clk(clock));  // open: clr
  Register #(.width(16)) _7 (.D(Write_data), .en(and_8_out), .Q(_7_q), .clk(clock));  // open: clr
  and and_9 (and_9_out, decoder_1_out8, Write_enable);
  and and_10 (and_10_out, decoder_1_out9, Write_enable);
  and and_11 (and_11_out, decoder_1_out10, Write_enable);
  and and_12 (and_12_out, decoder_1_out11, Write_enable);
  and and_13 (and_13_out, decoder_1_out12, Write_enable);
  and and_14 (and_14_out, decoder_1_out13, Write_enable);
  and and_15 (and_15_out, decoder_1_out14, Write_enable);
  and and_16 (and_16_out, decoder_1_out15, Write_enable);
  Register #(.width(16)) _8 (.D(Write_data), .en(and_9_out), .Q(_8_q), .clk(clock));  // open: clr
  Register #(.width(16)) _9 (.D(Write_data), .en(and_10_out), .Q(_9_q), .clk(clock));  // open: clr
  Register #(.width(16)) _10 (.D(Write_data), .en(and_11_out), .Q(_10_q), .clk(clock));  // open: clr
  Register #(.width(16)) _11 (.D(Write_data), .en(and_12_out), .Q(_11_q), .clk(clock));  // open: clr
  Register #(.width(16)) _12 (.D(Write_data), .en(and_13_out), .Q(_12_q), .clk(clock));  // open: clr
  Register #(.width(16)) _13 (.D(Write_data), .en(and_14_out), .Q(_13_q), .clk(clock));  // open: clr
  Register #(.width(16)) _14 (.D(Write_data), .en(and_15_out), .Q(_14_q), .clk(clock));  // open: clr
  Register #(.width(16)) _15 (.D(Write_data), .en(and_16_out), .Q(_15_q), .clk(clock));  // open: clr
  Multiplexer #(.select(4), .width(16), .enable("false")) multiplexer_1 (
    .in0(_0_q), .in1(_1_q), .in2(_2_q), .in3(_3_q), .in4(_4_q), .in5(_5_q), .in6(_6_q), .in7(_7_q),
    .in8(_8_q), .in9(_9_q), .in10(_10_q), .in11(_11_q), .in12(_12_q), .in13(_13_q), .in14(_14_q),
    .in15(_15_q), .out(Rd_1), .sel(Select_Ra_1));
  Multiplexer #(.select(4), .width(16), .enable("false")) multiplexer_2 (
    .in0(_0_q), .in1(_1_q), .in2(_2_q), .in3(_3_q), .in4(_4_q), .in5(_5_q), .in6(_6_q), .in7(_7_q),
    .in8(_8_q), .in9(_9_q), .in10(_10_q), .in11(_11_q), .in12(_12_q), .in13(_13_q), .in14(_14_q),
    .in15(_15_q), .out(Rd_2), .sel(Select_Ra_2));
endmodule

module qw (
  input  in_1,
  input  in_2,
  input  [3:0] Write_Register,
  input  [15:0] Write_data,
  input  [3:0] Select_Rd_1,
  input  in_6,
  input  [3:0] Select_Rd_2,
  input  Write_enable,
  input  in_9,
  output [15:0] Rd_1,
  output [15:0] Rd_2
);

  wire and_1_out, and_2_out, and_3_out, and_4_out, and_5_out, and_6_out, and_7_out, and_8_out, and_9_out,
       and_10_out, and_11_out, and_12_out, and_13_out, and_14_out, and_15_out, and_16_out, decoder_1_out0,
       decoder_1_out1, decoder_1_out2, decoder_1_out3, decoder_1_out4, decoder_1_out5, decoder_1_out6,
       decoder_1_out7, decoder_1_out8, decoder_1_out9, decoder_1_out10, decoder_1_out11, decoder_1_out12,
       decoder_1_out13, decoder_1_out14, decoder_1_out15, undriven;
  wire [15:0] _1_q, _2_q, _3_q, _4_q, _5_q, _6_q, _7_q, _8_q, _9_q, _10_q, _11_q, _12_q, _13_q, _14_q, _15_q,
       register_1_q, undriven_2, undriven_3, undriven_4, undriven_5, undriven_6, undriven_7, undriven_8,
       undriven_9, undriven_10, undriven_11, undriven_12, undriven_13, undriven_14, undriven_15, undriven_16,
       undriven_17;

  Decoder #(.select(4)) decoder_1 (
    .out0(decoder_1_out0), .out1(decoder_1_out1), .out2(decoder_1_out2), .out3(decoder_1_out3),
    .out4(decoder_1_out4), .out5(decoder_1_out5), .out6(decoder_1_out6), .out7(decoder_1_out7),
    .out8(decoder_1_out8), .out9(decoder_1_out9), .out10(decoder_1_out10), .out11(decoder_1_out11),
    .out12(decoder_1_out12), .out13(decoder_1_out13), .out14(decoder_1_out14), .out15(decoder_1_out15),
    .sel(Write_Register), .en(in_1));
  and and_1 (and_1_out, decoder_1_out0, Write_enable);
  and and_2 (and_2_out, decoder_1_out1, Write_enable);
  and and_3 (and_3_out, decoder_1_out2, Write_enable);
  and and_4 (and_4_out, decoder_1_out3, Write_enable);
  and and_5 (and_5_out, decoder_1_out4, Write_enable);
  and and_6 (and_6_out, decoder_1_out5, Write_enable);
  and and_7 (and_7_out, decoder_1_out6, Write_enable);
  and and_8 (and_8_out, decoder_1_out7, Write_enable);
  Register #(.width(16)) register_1 (.D(Write_data), .en(and_1_out), .Q(register_1_q), .clk(undriven));  // open: clr
  Register #(.width(16)) _1 (.D(Write_data), .en(and_2_out), .Q(_1_q), .clk(undriven));  // open: clr
  Register #(.width(16)) _2 (.D(Write_data), .en(and_3_out), .Q(_2_q), .clk(undriven));  // open: clr
  Register #(.width(16)) _3 (.D(Write_data), .en(and_4_out), .Q(_3_q), .clk(undriven));  // open: clr
  Register #(.width(16)) _4 (.D(Write_data), .en(and_5_out), .Q(_4_q), .clk(undriven));  // open: clr
  Register #(.width(16)) _5 (.D(Write_data), .en(and_6_out), .Q(_5_q), .clk(undriven));  // open: clr
  Register #(.width(16)) _6 (.D(Write_data), .en(and_7_out), .Q(_6_q), .clk(undriven));  // open: clr
  Register #(.width(16)) _7 (.D(Write_data), .en(and_8_out), .Q(_7_q), .clk(undriven));  // open: clr
  and and_9 (and_9_out, decoder_1_out8, Write_enable);
  and and_10 (and_10_out, decoder_1_out9, Write_enable);
  and and_11 (and_11_out, decoder_1_out10, Write_enable);
  and and_12 (and_12_out, decoder_1_out11, Write_enable);
  and and_13 (and_13_out, decoder_1_out12, Write_enable);
  and and_14 (and_14_out, decoder_1_out13, Write_enable);
  and and_15 (and_15_out, decoder_1_out14, Write_enable);
  and and_16 (and_16_out, decoder_1_out15, Write_enable);
  Register #(.width(16)) _8 (.D(Write_data), .en(and_9_out), .Q(_8_q), .clk(undriven));  // open: clr
  Register #(.width(16)) _9 (.D(Write_data), .en(and_10_out), .Q(_9_q), .clk(undriven));  // open: clr
  Register #(.width(16)) _10 (.D(Write_data), .en(and_11_out), .Q(_10_q), .clk(undriven));  // open: clr
  Register #(.width(16)) _11 (.D(Write_data), .en(and_12_out), .Q(_11_q), .clk(undriven));  // open: clr
  Register #(.width(16)) _12 (.D(Write_data), .en(and_13_out), .Q(_12_q), .clk(undriven));  // open: clr
  Register #(.width(16)) _13 (.D(Write_data), .en(and_14_out), .Q(_13_q), .clk(undriven));  // open: clr
  Register #(.width(16)) _14 (.D(Write_data), .en(and_15_out), .Q(_14_q), .clk(undriven));  // open: clr
  Register #(.width(16)) _15 (.D(Write_data), .en(and_16_out), .Q(_15_q), .clk(undriven));  // open: clr
  Multiplexer #(.select(4), .width(16)) multiplexer_1 (
    .in0(register_1_q), .in1(_1_q), .in2(_2_q), .in3(_3_q), .in4(_4_q), .in5(_5_q), .in6(_6_q), .in7(_7_q),
    .in8(_8_q), .in9(_9_q), .in10(_10_q), .in11(_11_q), .in12(_12_q), .in13(_13_q), .in14(_14_q),
    .in15(_15_q), .out(Rd_1), .sel(Select_Rd_1), .en(in_2));
  Multiplexer #(.select(4), .width(16)) multiplexer_2 (
    .in0(undriven_17), .in1(undriven_16), .in2(undriven_15), .in3(undriven_14), .in4(undriven_13),
    .in5(undriven_12), .in6(undriven_11), .in7(undriven_10), .in8(undriven_9), .in9(undriven_8),
    .in10(undriven_7), .in11(undriven_6), .in12(undriven_5), .in13(undriven_3), .in14(undriven_2),
    .in15(undriven_4), .out(Rd_2), .sel(Select_Rd_2), .en(in_6));
endmodule

module program_counter (
  input  [15:0] in_1
);

  wire CLK_out;
  wire [15:0] adder_1_out, counter_1_q;

  Adder #(.width(16)) adder_1 (.a(counter_1_q), .b(in_1), .out(adder_1_out));  // open: cin, cout
  Counter #(.width(16), .max('hffff)) counter_1 (
    .D(adder_1_out), .Q(counter_1_q), .clk(CLK_out));  // open: load, count, carry, clr
  Clock CLK (.out(CLK_out));
endmodule

module cu (
  input  a,
  input  b,
  input  c,
  input  d,
  output y1,
  output y2,
  output y43,
  output y4,
  output y5,
  output y6,
  output y7
);

  wire and_2_out, and_3_out, and_4_out, and_5_out, and_6_out, and_7_out, and_8_out, and_9_out, and_10_out,
       and_11_out, and_12_out, not_1_out, not_2_out, not_3_out, not_4_out, not_5_out, not_6_out, not_7_out,
       not_8_out, not_9_out, not_10_out, not_11_out, not_12_out, not_13_out, not_14_out, not_15_out,
       not_16_out;

  not not_1 (not_1_out, a);
  and and_1 (y1, not_1_out, d);
  not not_2 (not_2_out, b);
  and and_2 (and_2_out, not_2_out, not_3_out);
  not not_3 (not_3_out, d);
  and and_3 (and_3_out, c, not_4_out);
  not not_4 (not_4_out, d);
  not not_5 (not_5_out, a);
  and and_4 (and_4_out, not_5_out, not_6_out, not_7_out);
  not not_6 (not_6_out, b);
  not not_7 (not_7_out, c);
  not not_8 (not_8_out, a);
  and and_5 (and_5_out, not_8_out, not_9_out);
  not not_9 (not_9_out, d);
  and and_6 (and_6_out, a, d);
  not not_10 (not_10_out, b);
  and and_7 (and_7_out, not_10_out, not_11_out);
  not not_11 (not_11_out, c);
  not not_12 (not_12_out, a);
  and and_8 (and_8_out, not_12_out, not_13_out);
  not not_13 (not_13_out, d);
  and and_9 (and_9_out, a, d);
  not not_14 (not_14_out, b);
  not not_15 (not_15_out, c);
  and and_10 (and_10_out, not_14_out, not_15_out, not_16_out);
  not not_16 (not_16_out, d);
  and and_11 (and_11_out, c, d);
  and and_12 (and_12_out, b, d);
  or or_1 (y2, and_2_out, and_3_out, a);
  or or_2 (y43, and_4_out, d);
  or or_3 (y4, and_5_out, and_6_out);
  or or_4 (y5, and_7_out, d);
  or or_5 (y6, and_8_out, and_9_out);
  or or_6 (y7, and_10_out, and_11_out, and_12_out, a);
endmodule

module Control_Unit_old (
  input  I_15,
  input  I_14,
  input  I_13,
  input  I_12,
  output Alu_Select1,
  output Alu_Select2,
  output Alu_select3,
  output mem_write,
  output Src_A_Select,
  output Wd_select,
  output reg_write
);

  wire nand_1_out, nand_2_out, nand_3_out;

  nand nand_1 (nand_1_out, I_14, I_14);
  nand nand_2 (nand_2_out, I_15, I_15);
  nand nand_3 (nand_3_out, I_15, I_12);
  nand nand_4 (Src_A_Select, I_15, I_15);
  nand nand_5 (Wd_select, I_15, I_15);
  nand nand_6 (reg_write, I_15, I_15);
  nand nand_7 (Alu_Select1, nand_1_out, nand_2_out);
  nand nand_8 (mem_write, nand_3_out, nand_3_out);

  assign Alu_Select2 = I_13;
  assign Alu_select3 = I_12;
endmodule

// control Unit
module control_unit (
  input  I_15,
  input  I_14,
  input  I_13,
  input  I_12,
  output Alu_Select0,
  output Alu_Select1,
  output Alu_Select2,
  output Alu_select3,
  output mem_write,
  output Src_A_Select,
  output Wd_select,
  output reg_write
);

  wire nand_1_out, nand_2_out, nand_3_out;

  nand nand_1 (nand_1_out, I_14, I_14);
  nand nand_2 (nand_2_out, I_15, I_15);
  nand nand_3 (nand_3_out, I_15, I_12);
  nand nand_4 (Src_A_Select, I_15, I_15);
  nand nand_5 (Wd_select, I_15, I_15);
  nand nand_6 (reg_write, I_15, I_15);
  nand nand_7 (Alu_Select1, nand_1_out, nand_2_out);
  nand nand_8 (mem_write, nand_3_out, nand_3_out);

  assign Alu_Select2 = I_13;
  assign Alu_select3 = I_12;
endmodule

module control_unit_2 (
  input  I_15,
  input  I_14,
  input  I_13,
  input  I_12,
  output Alu_Select0,
  output Alu_Select1,
  output Alu_Select2,
  output Alu_select3,
  output mem_write,
  output Src_A_Select,
  output Wd_select,
  output reg_write
);

  wire nand_1_out, nand_2_out, nand_3_out, nand_4_out;

  nand nand_1 (nand_1_out, I_15, I_12);
  nand nand_2 (nand_2_out, I_14, I_14);
  nand nand_3 (nand_3_out, I_15, I_15);
  nand nand_4 (nand_4_out, I_15, I_12);
  nand nand_5 (Src_A_Select, I_15, I_15);
  nand nand_6 (Wd_select, I_15, I_15);
  nand nand_7 (reg_write, I_15, I_15);
  nand nand_8 (Alu_Select0, nand_1_out, nand_1_out);
  nand nand_9 (Alu_Select1, nand_2_out, nand_3_out);
  nand nand_10 (mem_write, nand_4_out, nand_4_out);

  assign Alu_Select2 = I_13;
  assign Alu_select3 = I_12;
endmodule

module control_mem_1 (
  input  I_15,
  input  I_14,
  input  I_13,
  input  I_12,
  output Alu_Select0,
  output Alu_Select1,
  output Alu_Select2,
  output Alu_select3,
  output mem_write,
  output Src_A_Select,
  output Wd_select,
  output reg_write
);

  wire nand_1_out, nand_2_out, nand_3_out;

  nand nand_1 (nand_1_out, I_15, I_12);
  nand nand_2 (nand_2_out, I_14, I_14);
  nand nand_3 (nand_3_out, I_15, I_15);
  nand nand_4 (Src_A_Select, I_15, I_15);
  nand nand_5 (Wd_select, I_15, I_15);
  nand nand_6 (reg_write, I_15, I_15);
  nand nand_7 (Alu_Select0, nand_1_out, nand_1_out);
  nand nand_8 (Alu_Select1, nand_2_out, nand_3_out);

  assign Alu_Select2 = I_13;
  assign Alu_select3 = I_12;
  assign mem_write = I_15;
endmodule

// controo_mem_1_reg
module control_mem_1_reg (
  input  I_15,
  input  I_14,
  input  I_13,
  input  I_12,
  output Alu_Select0,
  output Alu_Select1,
  output Alu_Select2,
  output Alu_select3,
  output mem_write,
  output Src_A_Select,
  output Wd_select,
  output reg_write
);

  wire nand_1_out, nand_2_out, nand_3_out, nand_4_out, nand_7_out, nand_8_out, nand_9_out, nand_12_out;

  nand nand_1 (nand_1_out, I_15, I_12);
  nand nand_2 (nand_2_out, I_15, I_12);
  nand nand_3 (nand_3_out, I_14, I_14);
  nand nand_4 (nand_4_out, I_15, I_15);
  nand nand_5 (Src_A_Select, I_15, I_15);
  nand nand_6 (Wd_select, I_15, I_15);
  nand nand_7 (nand_7_out, I_14, I_14);
  nand nand_8 (nand_8_out, I_13, I_13);
  nand nand_9 (nand_9_out, I_12, I_12);
  nand nand_10 (Alu_Select0, nand_1_out, nand_2_out);
  nand nand_11 (Alu_Select1, nand_3_out, nand_4_out);
  nand nand_12 (nand_12_out, nand_7_out, nand_8_out, nand_9_out);
  nand nand_13 (reg_write, I_15, nand_12_out);

  assign Alu_Select2 = I_13;
  assign Alu_select3 = I_12;
  assign mem_write = I_15;
endmodule

module control_mem_1_load (
  input  I_15,
  input  I_14,
  input  I_13,
  input  I_12,
  output Alu_Select0,
  output Alu_Select1,
  output Alu_Select2,
  output Alu_select3,
  output load,
  output Src_A_Select,
  output Wd_select,
  output reg_write
);

  wire nand_1_out, nand_2_out, nand_3_out, nand_4_out, nand_7_out, nand_8_out, nand_9_out, nand_12_out;

  nand nand_1 (nand_1_out, I_15, I_12);
  nand nand_2 (nand_2_out, I_15, I_12);
  nand nand_3 (nand_3_out, I_14, I_14);
  nand nand_4 (nand_4_out, I_15, I_15);
  nand nand_5 (Src_A_Select, I_15, I_15);
  nand nand_6 (Wd_select, I_15, I_15);
  nand nand_7 (nand_7_out, I_14, I_14);
  nand nand_8 (nand_8_out, I_13, I_13);
  nand nand_9 (nand_9_out, I_12, I_12);
  nand nand_10 (Alu_Select0, nand_1_out, nand_2_out);
  nand nand_11 (Alu_Select1, nand_3_out, nand_4_out);
  nand nand_12 (nand_12_out, nand_7_out, nand_8_out, nand_9_out);
  nand nand_13 (reg_write, I_15, nand_12_out);

  assign Alu_Select2 = I_13;
  assign Alu_select3 = I_12;
  assign load = I_15;
endmodule

module control_offset (
  input  I_15,
  input  I_14,
  input  I_13,
  input  I_12,
  output Alu_Select0,
  output Alu_Select1,
  output Alu_Select2,
  output Alu_select3,
  output load,
  output Src_A_Select,
  output Wd_select,
  output reg_write,
  output offset_select
);

  wire nand_1_out, nand_2_out, nand_3_out, nand_4_out, nand_5_out, nand_6_out, nand_9_out, nand_10_out,
       nand_11_out, nand_14_out, nand_15_out, nand_16_out, nand_17_out, nand_18_out, nand_19_out, nand_20_out;

  nand nand_1 (nand_1_out, I_15, I_13, I_12);
  nand nand_2 (nand_2_out, I_15, I_14, I_12);
  nand nand_3 (nand_3_out, I_14, I_14);
  nand nand_4 (nand_4_out, I_15, I_15);
  nand nand_5 (nand_5_out, I_15, I_15);
  nand nand_6 (nand_6_out, I_12, I_12);
  nand nand_7 (Src_A_Select, I_15, I_15);
  nand nand_8 (Wd_select, I_15, I_15);
  nand nand_9 (nand_9_out, I_14, I_14);
  nand nand_10 (nand_10_out, I_13, I_13);
  nand nand_11 (nand_11_out, I_12, I_12);
  nand nand_12 (Alu_Select0, nand_1_out, nand_2_out);
  nand nand_13 (Alu_Select1, nand_3_out, nand_4_out);
  nand nand_14 (nand_14_out, nand_5_out, I_12);
  nand nand_15 (nand_15_out, I_13, I_12);
  nand nand_16 (nand_16_out, I_14, I_12);
  nand nand_17 (nand_17_out, I_15, nand_6_out);
  nand nand_18 (nand_18_out, I_15, I_13);
  nand nand_19 (nand_19_out, I_15, I_14);
  nand nand_20 (nand_20_out, nand_9_out, nand_10_out, nand_11_out);
  nand nand_21 (Alu_select3, nand_14_out, nand_15_out, nand_16_out);
  nand nand_22 (load, nand_17_out, nand_18_out, nand_19_out);
  nand nand_23 (reg_write, I_15, nand_20_out);

  assign Alu_Select2 = I_13;
  assign offset_select = I_12;
endmodule

module cu_offset_2 (
  input  I_15,
  input  I_14,
  input  I_13,
  input  I_12,
  output Alu_Select0,
  output Alu_Select1,
  output Alu_Select2,
  output Alu_select3,
  output load,
  output Src_A_Select,
  output Wd_select,
  output reg_write,
  output offset_select
);

  wire nand_1_out, nand_2_out, nand_3_out, nand_4_out, nand_5_out, nand_8_out, nand_9_out, nand_10_out,
       nand_13_out, nand_14_out, nand_15_out, nand_16_out;

  nand nand_1 (nand_1_out, I_15, I_13, I_12);
  nand nand_2 (nand_2_out, I_15, I_14, I_12);
  nand nand_3 (nand_3_out, I_14, I_14);
  nand nand_4 (nand_4_out, I_15, I_15);
  nand nand_5 (nand_5_out, I_15, I_15);
  nand nand_6 (Src_A_Select, I_15, I_15);
  nand nand_7 (Wd_select, I_15, I_15);
  nand nand_8 (nand_8_out, I_14, I_14);
  nand nand_9 (nand_9_out, I_13, I_13);
  nand nand_10 (nand_10_out, I_12, I_12);
  nand nand_11 (Alu_Select0, nand_1_out, nand_2_out);
  nand nand_12 (Alu_Select1, nand_3_out, nand_4_out);
  nand nand_13 (nand_13_out, nand_5_out, I_12);
  nand nand_14 (nand_14_out, I_13, I_12);
  nand nand_15 (nand_15_out, I_14, I_12);
  nand nand_16 (nand_16_out, nand_8_out, nand_9_out, nand_10_out);
  nand nand_17 (Alu_select3, nand_13_out, nand_14_out, nand_15_out);
  nand nand_18 (reg_write, I_15, nand_16_out);

  assign Alu_Select2 = I_13;
  assign load = I_15;
  assign offset_select = I_12;
endmodule

module cu_offset_3 (
  input  I_15,
  input  I_14,
  input  I_13,
  input  I_12,
  output Alu_Select0,
  output Alu_Select1,
  output Alu_Select2,
  output Alu_select3,
  output load,
  output Src_A_Select,
  output Wd_select,
  output reg_write,
  output offset_select
);

  wire nand_1_out, nand_2_out, nand_3_out, nand_4_out, nand_5_out, nand_6_out, nand_8_out, nand_9_out,
       nand_10_out, nand_11_out, nand_12_out, nand_15_out, nand_16_out, nand_17_out, nand_18_out,
       nand_19_out, nand_20_out, nand_21_out, nand_22_out;

  nand nand_1 (nand_1_out, I_15, I_13, I_12);
  nand nand_2 (nand_2_out, I_15, I_14, I_12);
  nand nand_3 (nand_3_out, I_14, I_14);
  nand nand_4 (nand_4_out, I_15, I_15);
  nand nand_5 (nand_5_out, I_15, I_15);
  nand nand_6 (nand_6_out, I_12, I_12);
  nand nand_7 (Src_A_Select, I_15, I_15);
  nand nand_8 (nand_8_out, I_14, I_14);
  nand nand_9 (nand_9_out, I_13, I_13);
  nand nand_10 (nand_10_out, I_12, I_12);
  nand nand_11 (nand_11_out, I_14, I_14);
  nand nand_12 (nand_12_out, I_13, I_13);
  nand nand_13 (Alu_Select0, nand_1_out, nand_2_out);
  nand nand_14 (Alu_Select1, nand_3_out, nand_4_out);
  nand nand_15 (nand_15_out, nand_5_out, I_12);
  nand nand_16 (nand_16_out, I_13, I_12);
  nand nand_17 (nand_17_out, I_14, I_12);
  nand nand_18 (nand_18_out, I_15, nand_6_out);
  nand nand_19 (nand_19_out, I_15, I_13);
  nand nand_20 (nand_20_out, I_15, I_14);
  nand nand_21 (nand_21_out, I_15, nand_8_out, nand_9_out, nand_10_out);
  nand nand_22 (nand_22_out, nand_11_out, nand_12_out);
  nand nand_23 (Alu_select3, nand_15_out, nand_16_out, nand_17_out);
  nand nand_24 (load, nand_18_out, nand_19_out, nand_20_out);
  nand nand_25 (Wd_select, nand_21_out, nand_21_out);
  nand nand_26 (reg_write, I_15, nand_22_out);
  main main_1 ();  // open: in_1

  assign Alu_Select2 = I_13;
  assign offset_select = I_12;
endmodule

module control_offset_6 (
  input  I_15,
  input  I_14,
  input  I_13,
  input  I_12,
  output Alu_Select0,
  output Alu_Select1,
  output Alu_Select2,
  output Alu_select3,
  output load,
  output Src_A_Select,
  output Wd_select,
  output reg_write,
  output offset_select
);

  wire nand_1_out, nand_2_out, nand_3_out, nand_4_out, nand_5_out, nand_6_out, nand_8_out, nand_9_out,
       nand_10_out, nand_11_out, nand_12_out, nand_13_out, nand_16_out, nand_17_out, nand_18_out,
       nand_19_out, nand_20_out, nand_21_out, nand_22_out, nand_23_out;

  nand nand_1 (nand_1_out, I_15, I_13, I_12);
  nand nand_2 (nand_2_out, I_15, I_14, I_12);
  nand nand_3 (nand_3_out, I_14, I_14);
  nand nand_4 (nand_4_out, I_15, I_15);
  nand nand_5 (nand_5_out, I_15, I_15);
  nand nand_6 (nand_6_out, I_12, I_12);
  nand nand_7 (Src_A_Select, I_15, I_15);
  nand nand_8 (nand_8_out, I_14, I_14);
  nand nand_9 (nand_9_out, I_13, I_13);
  nand nand_10 (nand_10_out, I_14, I_14);
  nand nand_11 (nand_11_out, I_13, I_13);
  nand nand_12 (nand_12_out, I_12, I_12);
  nand nand_13 (nand_13_out, I_12, I_12);
  nand nand_14 (Alu_Select0, nand_1_out, nand_2_out);
  nand nand_15 (Alu_Select1, nand_3_out, nand_4_out);
  nand nand_16 (nand_16_out, nand_5_out, I_12);
  nand nand_17 (nand_17_out, I_13, I_12);
  nand nand_18 (nand_18_out, I_14, I_12);
  nand nand_19 (nand_19_out, I_15, nand_6_out);
  nand nand_20 (nand_20_out, I_15, I_13);
  nand nand_21 (nand_21_out, I_15, I_14);
  nand nand_22 (nand_22_out, I_15, nand_8_out, nand_9_out);
  nand nand_23 (nand_23_out, nand_10_out, nand_11_out, nand_12_out);
  nand nand_24 (offset_select, I_15, nand_13_out);
  nand nand_25 (Alu_select3, nand_16_out, nand_17_out, nand_18_out);
  nand nand_26 (load, nand_19_out, nand_20_out, nand_21_out);
  nand nand_27 (Wd_select, nand_22_out, nand_22_out);
  nand nand_28 (reg_write, I_15, nand_23_out);

  assign Alu_Select2 = I_13;
endmodule

module final_cu (
  input  I_15,
  input  I_14,
  input  I_13,
  input  I_12,
  output Alu_Select0,
  output Alu_Select1,
  output Alu_Select2,
  output Alu_select3,
  output load,
  output Src_A_Select,
  output Wd_select,
  output reg_write,
  output offset_select
);

  wire nand_1_out, nand_2_out, nand_3_out, nand_4_out, nand_5_out, nand_6_out, nand_9_out, nand_10_out,
       nand_11_out, nand_14_out, nand_15_out, nand_16_out, nand_17_out, nand_18_out, nand_19_out, nand_20_out;

  nand nand_1 (nand_1_out, I_15, I_13, I_12);
  nand nand_2 (nand_2_out, I_15, I_14, I_12);
  nand nand_3 (nand_3_out, I_14, I_14);
  nand nand_4 (nand_4_out, I_15, I_15);
  nand nand_5 (nand_5_out, I_15, I_15);
  nand nand_6 (nand_6_out, I_12, I_12);
  nand nand_7 (Src_A_Select, I_15, I_15);
  nand nand_8 (Wd_select, I_15, I_15);
  nand nand_9 (nand_9_out, I_14, I_14);
  nand nand_10 (nand_10_out, I_13, I_13);
  nand nand_11 (nand_11_out, I_12, I_12);
  nand nand_12 (Alu_Select0, nand_1_out, nand_2_out);
  nand nand_13 (Alu_Select1, nand_3_out, nand_4_out);
  nand nand_14 (nand_14_out, nand_5_out, I_12);
  nand nand_15 (nand_15_out, I_13, I_12);
  nand nand_16 (nand_16_out, I_14, I_12);
  nand nand_17 (nand_17_out, I_15, nand_6_out);
  nand nand_18 (nand_18_out, I_15, I_13);
  nand nand_19 (nand_19_out, I_15, I_14);
  nand nand_20 (nand_20_out, nand_9_out, nand_10_out, nand_11_out);
  nand nand_21 (Alu_select3, nand_14_out, nand_15_out, nand_16_out);
  nand nand_22 (load, nand_17_out, nand_18_out, nand_19_out);
  nand nand_23 (reg_write, I_15, nand_20_out);

  assign Alu_Select2 = I_13;
  assign offset_select = I_12;
endmodule

module final_cu_1 (
  input  I_15,
  input  I_14,
  input  I_13,
  input  I_12,
  output Alu_Select0,
  output Alu_Select1,
  output Alu_Select2,
  output Alu_select3,
  output store,
  output Src_A_Select,
  output Wd_select,
  output reg_write,
  output offset_select
);

  wire nand_1_out, nand_2_out, nand_3_out, nand_4_out, nand_5_out, nand_6_out, nand_9_out, nand_10_out,
       nand_11_out, nand_14_out, nand_15_out, nand_16_out, nand_18_out;

  nand nand_1 (nand_1_out, I_15, I_13, I_12);
  nand nand_2 (nand_2_out, I_15, I_14, I_12);
  nand nand_3 (nand_3_out, I_14, I_14);
  nand nand_4 (nand_4_out, I_15, I_15);
  nand nand_5 (nand_5_out, I_15, I_15);
  nand nand_6 (nand_6_out, I_15, I_12);
  nand nand_7 (Src_A_Select, I_15, I_15);
  nand nand_8 (Wd_select, I_15, I_15);
  nand nand_9 (nand_9_out, I_14, I_14);
  nand nand_10 (nand_10_out, I_13, I_13);
  nand nand_11 (nand_11_out, I_12, I_12);
  nand nand_12 (Alu_Select0, nand_1_out, nand_2_out);
  nand nand_13 (Alu_Select1, nand_3_out, nand_4_out);
  nand nand_14 (nand_14_out, nand_5_out, I_12);
  nand nand_15 (nand_15_out, I_13, I_12);
  nand nand_16 (nand_16_out, I_14, I_12);
  nand nand_17 (store, nand_6_out, nand_6_out);
  nand nand_18 (nand_18_out, nand_9_out, nand_10_out, nand_11_out);
  nand nand_19 (Alu_select3, nand_14_out, nand_15_out, nand_16_out);
  nand nand_20 (reg_write, I_15, nand_18_out);

  assign Alu_Select2 = I_13;
  assign offset_select = I_12;
endmodule

module final_cu_2 (
  input  I_15,
  input  I_14,
  input  I_13,
  input  I_12,
  output Alu_Select0,
  output Alu_Select1,
  output Alu_Select2,
  output Alu_select3,
  output store,
  output Src_A_Select,
  output Wd_select,
  output reg_write,
  output offset_select,
  output Branch,
  output Branch_select
);

  wire and_1_out, and_2_out, and_3_out, and_4_out, nand_1_out, nand_2_out, nand_3_out, nand_4_out,
       nand_5_out, nand_6_out, nand_7_out, nand_8_out, nand_9_out, nand_10_out, nand_11_out, nand_12_out,
       nand_13_out, nand_14_out, nand_15_out, nand_16_out, nand_19_out, nand_20_out, nand_21_out,
       nand_22_out, nand_23_out, nand_24_out, nand_25_out, nand_26_out, nand_27_out, nand_28_out,
       nand_29_out, nand_30_out, not_1_out, not_2_out, not_3_out, not_4_out, not_5_out, not_6_out;

  nand nand_1 (nand_1_out, I_15, I_14, I_12);
  nand nand_2 (nand_2_out, I_15, I_14, I_12);
  nand nand_3 (nand_3_out, I_14, I_14);
  nand nand_4 (nand_4_out, I_15, I_15);
  nand nand_5 (nand_5_out, I_15, I_15);
  nand nand_6 (nand_6_out, I_15, I_15);
  nand nand_7 (nand_7_out, I_14, I_14);
  nand nand_8 (nand_8_out, I_13, I_13);
  nand nand_9 (nand_9_out, I_14, I_14);
  nand nand_10 (nand_10_out, I_14, I_14);
  nand nand_11 (nand_11_out, I_14, I_14);
  nand nand_12 (nand_12_out, I_13, I_13);
  nand nand_13 (nand_13_out, I_12, I_12);
  nand nand_14 (nand_14_out, I_14, I_14);
  nand nand_15 (nand_15_out, I_15, I_13);
  nand nand_16 (nand_16_out, I_15, I_13);
  not not_1 (not_1_out, I_15);
  not not_2 (not_2_out, I_12);
  not not_3 (not_3_out, I_14);
  not not_4 (not_4_out, I_12);
  not not_5 (not_5_out, I_12);
  not not_6 (not_6_out, I_13);
  nand nand_17 (Alu_Select0, nand_1_out, nand_2_out);
  nand nand_18 (Alu_Select1, nand_3_out, nand_4_out);
  nand nand_19 (nand_19_out, nand_5_out, I_13);
  nand nand_20 (nand_20_out, I_14, I_13);
  nand nand_21 (nand_21_out, nand_6_out, I_12);
  nand nand_22 (nand_22_out, I_14, I_12);
  nand nand_23 (nand_23_out, I_15, nand_7_out, I_13);
  nand nand_24 (nand_24_out, I_15, nand_8_out, I_12);
  nand nand_25 (nand_25_out, I_15, I_14, I_12);
  nand nand_26 (nand_26_out, nand_9_out, I_13);
  nand nand_27 (nand_27_out, nand_10_out, I_13);
  nand nand_28 (nand_28_out, nand_11_out, nand_12_out, nand_13_out);
  nand nand_29 (nand_29_out, I_12, I_12);
  nand nand_30 (nand_30_out, I_15, nand_14_out, I_13);
  nand nand_31 (Branch, nand_15_out, nand_16_out);
  and and_1 (and_1_out, not_1_out, not_2_out);
  and and_2 (and_2_out, not_3_out, not_4_out);
  and and_3 (and_3_out, I_13, not_5_out);
  and and_4 (and_4_out, I_15, I_14, not_6_out, I_12);
  nand nand_32 (Alu_Select2, nand_19_out, nand_20_out);
  nand nand_33 (Alu_select3, nand_21_out, nand_22_out, nand_23_out);
  nand nand_34 (store, nand_24_out, nand_25_out);
  nand nand_35 (Src_A_Select, I_15, nand_26_out);
  nand nand_36 (Wd_select, I_15, nand_27_out);
  nand nand_37 (reg_write, I_15, nand_28_out);
  nand nand_38 (offset_select, nand_29_out, nand_30_out);
  or or_1 (Branch_select, and_1_out, and_2_out, and_3_out, and_4_out);
endmodule

module final_cu_3 (
  input  I_15,
  input  I_14,
  input  I_13,
  input  I_12,
  output Alu_Select0,
  output Alu_Select1,
  output Alu_Select2,
  output Alu_select3,
  output store,
  output Src_A_Select,
  output Wd_select,
  output reg_write,
  output offset_select,
  output Branch,
  output Branch_select
);

  wire nand_1_out, nand_2_out, nand_3_out, nand_4_out, nand_5_out, nand_6_out, nand_7_out, nand_8_out,
       nand_9_out, nand_10_out, nand_11_out, nand_12_out, nand_13_out, nand_14_out, nand_15_out, nand_16_out,
       nand_17_out, nand_20_out, nand_21_out, nand_22_out, nand_23_out, nand_24_out, nand_25_out,
       nand_26_out, nand_27_out, nand_28_out, nand_29_out, nand_30_out, nand_31_out, nand_33_out;

  nand nand_1 (nand_1_out, I_15, I_14, I_12);
  nand nand_2 (nand_2_out, I_15, I_14, I_12);
  nand nand_3 (nand_3_out, I_14, I_14);
  nand nand_4 (nand_4_out, I_15, I_15);
  nand nand_5 (nand_5_out, I_15, I_15);
  nand nand_6 (nand_6_out, I_15, I_15);
  nand nand_7 (nand_7_out, I_14, I_14);
  nand nand_8 (nand_8_out, I_13, I_13);
  nand nand_9 (nand_9_out, I_14, I_14);
  nand nand_10 (nand_10_out, I_14, I_14);
  nand nand_11 (nand_11_out, I_14, I_14);
  nand nand_12 (nand_12_out, I_13, I_13);
  nand nand_13 (nand_13_out, I_12, I_12);
  nand nand_14 (nand_14_out, I_14, I_14);
  nand nand_15 (nand_15_out, I_15, I_13);
  nand nand_16 (nand_16_out, I_15, I_13);
  nand nand_17 (nand_17_out, I_14, I_14);
  nand nand_18 (Alu_Select0, nand_1_out, nand_2_out);
  nand nand_19 (Alu_Select1, nand_3_out, nand_4_out);
  nand nand_20 (nand_20_out, nand_5_out, I_13);
  nand nand_21 (nand_21_out, I_14, I_13);
  nand nand_22 (nand_22_out, nand_6_out, I_12);
  nand nand_23 (nand_23_out, I_14, I_12);
  nand nand_24 (nand_24_out, I_15, nand_7_out, I_13);
  nand nand_25 (nand_25_out, I_15, nand_8_out, I_12);
  nand nand_26 (nand_26_out, I_15, I_14, I_12);
  nand nand_27 (nand_27_out, nand_9_out, I_13);
  nand nand_28 (nand_28_out, nand_10_out, I_13);
  nand nand_29 (nand_29_out, nand_11_out, nand_12_out, nand_13_out);
  nand nand_30 (nand_30_out, I_12, I_12);
  nand nand_31 (nand_31_out, I_15, nand_14_out, I_13);
  nand nand_32 (Branch, nand_15_out, nand_16_out);
  nand nand_33 (nand_33_out, nand_17_out, I_12);
  nand nand_34 (Alu_Select2, nand_20_out, nand_21_out);
  nand nand_35 (Alu_select3, nand_22_out, nand_23_out, nand_24_out);
  nand nand_36 (store, nand_25_out, nand_26_out);
  nand nand_37 (Src_A_Select, I_15, nand_27_out);
  nand nand_38 (Wd_select, I_15, nand_28_out);
  nand nand_39 (reg_write, I_15, nand_29_out);
  nand nand_40 (offset_select, nand_30_out, nand_31_out);
  nand nand_41 (Branch_select, nand_33_out, nand_33_out);
endmodule

module final_cu_4 (
  input  I_15,
  input  I_14,
  input  I_13,
  input  I_12,
  output Alu_Select0,
  output Alu_Select1,
  output Alu_Select2,
  output Alu_select3,
  output store,
  output Src_A_Select,
  output Wd_select,
  output reg_write,
  output offset_select,
  output Branch,
  output Branch_select,
  output Jump_select
);

  wire nand_1_out, nand_2_out, nand_3_out, nand_4_out, nand_5_out, nand_6_out, nand_7_out, nand_8_out,
       nand_9_out, nand_10_out, nand_11_out, nand_12_out, nand_13_out, nand_14_out, nand_15_out, nand_16_out,
       nand_17_out, nand_18_out, nand_19_out, nand_20_out, nand_21_out, nand_22_out, nand_23_out,
       nand_24_out, nand_26_out, nand_27_out, nand_28_out, nand_29_out, nand_30_out, nand_31_out,
       nand_32_out, nand_33_out, nand_34_out, nand_35_out, nand_36_out, nand_37_out, nand_38_out,
       nand_39_out, nand_40_out, nand_41_out, nand_43_out;

  nand nand_1 (nand_1_out, I_13, I_13);
  nand nand_2 (nand_2_out, I_14, I_14);
  nand nand_3 (nand_3_out, I_15, I_15);
  nand nand_4 (nand_4_out, I_15, I_15);
  nand nand_5 (nand_5_out, I_12, I_12);
  nand nand_6 (nand_6_out, I_15, I_15);
  nand nand_7 (nand_7_out, I_14, I_14);
  nand nand_8 (nand_8_out, I_13, I_13);
  nand nand_9 (nand_9_out, I_13, I_13);
  nand nand_10 (nand_10_out, I_14, I_14);
  nand nand_11 (nand_11_out, I_13, I_13);
  nand nand_12 (nand_12_out, I_12, I_12);
  nand nand_13 (nand_13_out, I_14, I_14);
  nand nand_14 (nand_14_out, I_13, I_13);
  nand nand_15 (nand_15_out, I_12, I_12);
  nand nand_16 (nand_16_out, I_14, I_14);
  nand nand_17 (nand_17_out, I_13, I_13);
  nand nand_18 (nand_18_out, I_12, I_12);
  nand nand_19 (nand_19_out, I_13, I_13);
  nand nand_20 (nand_20_out, I_15, I_13);
  nand nand_21 (nand_21_out, I_14, I_14);
  nand nand_22 (nand_22_out, I_15, I_14);
  nand nand_23 (nand_23_out, I_15, I_14, nand_1_out);
  nand nand_24 (nand_24_out, I_15, I_14, I_12);
  nand nand_25 (Alu_Select1, nand_2_out, nand_3_out);
  nand nand_26 (nand_26_out, nand_4_out, I_13);
  nand nand_27 (nand_27_out, I_14, I_13);
  nand nand_28 (nand_28_out, I_15, I_14, nand_5_out);
  nand nand_29 (nand_29_out, nand_6_out, I_12);
  nand nand_30 (nand_30_out, I_14, I_12);
  nand nand_31 (nand_31_out, I_15, nand_7_out, I_13);
  nand nand_32 (nand_32_out, I_15, I_14, nand_8_out);
  nand nand_33 (nand_33_out, I_15, nand_9_out, I_12);
  nand nand_34 (nand_34_out, I_15, I_14, I_12);
  nand nand_35 (nand_35_out, nand_10_out, I_13);
  nand nand_36 (nand_36_out, I_14, nand_11_out, nand_12_out);
  nand nand_37 (nand_37_out, nand_13_out, I_13);
  nand nand_38 (nand_38_out, I_14, nand_14_out, nand_15_out);
  nand nand_39 (nand_39_out, nand_16_out, nand_17_out, nand_18_out);
  nand nand_40 (nand_40_out, I_12, I_12);
  nand nand_41 (nand_41_out, I_14, nand_19_out);
  nand nand_42 (Branch, nand_20_out, nand_20_out);
  nand nand_43 (nand_43_out, nand_21_out, I_12);
  nand nand_44 (Jump_select, nand_22_out, nand_22_out);
  nand nand_45 (Alu_Select0, nand_23_out, nand_24_out);
  nand nand_46 (Alu_Select2, nand_26_out, nand_27_out, nand_28_out);
  nand nand_47 (Alu_select3, nand_29_out, nand_30_out, nand_31_out, nand_32_out);
  nand nand_48 (store, nand_33_out, nand_34_out);
  nand nand_49 (Src_A_Select, I_15, nand_35_out, nand_36_out);
  nand nand_50 (Wd_select, I_15, nand_37_out, nand_38_out);
  nand nand_51 (reg_write, I_15, nand_39_out);
  nand nand_52 (offset_select, nand_40_out, nand_41_out);
  nand nand_53 (Branch_select, nand_43_out, nand_43_out);
endmodule
